// Logisim project 16 x 16 Register.circ as structural Verilog: 3 circuits, main circuit 16 bit register
module _16_bit_register (
  input  [15:0] _16bit_input,
  input  clock,
  input  reset,
  output [15:0] out_4
);

  D_Flip_Flop d_ff_1 (.clk(clock), .D(_16bit_input[0]), .Q(out_4[0]), .reset(reset));  // open: Qn, preset, en
  D_Flip_Flop d_ff_2 (.clk(clock), .D(_16bit_input[1]), .Q(out_4[1]), .reset(reset));  // open: Qn, preset, en
  D_Flip_Flop d_ff_3 (.clk(clock), .D(_16bit_input[2]), .Q(out_4[2]), .reset(reset));  // open: Qn, preset, en
  D_Flip_Flop d_ff_4 (.clk(clock), .D(_16bit_input[3]), .Q(out_4[3]), .reset(reset));  // open: Qn, preset, en
  D_Flip_Flop d_ff_5 (.clk(clock), .D(_16bit_input[4]), .Q(out_4[4]), .reset(reset));  // open: Qn, preset, en
  D_Flip_Flop d_ff_6 (.clk(clock), .D(_16bit_input[5]), .Q(out_4[5]), .reset(reset));  // open: Qn, preset, en
  D_Flip_Flop d_ff_7 (.clk(clock), .D(_16bit_input[6]), .Q(out_4[6]), .reset(reset));  // open: Qn, preset, en
  D_Flip_Flop d_ff_8 (.clk(clock), .D(_16bit_input[7]), .Q(out_4[7]), .reset(reset));  // open: Qn, preset, en
  D_Flip_Flop d_ff_9 (.clk(clock), .D(_16bit_input[8]), .Q(out_4[8]), .reset(reset));  // open: Qn, preset, en
  D_Flip_Flop d_ff_10 (.clk(clock), .D(_16bit_input[9]), .Q(out_4[9]), .reset(reset));  // open: Qn, preset, en
  D_Flip_Flop d_ff_11 (.clk(clock), .D(_16bit_input[10]), .Q(out_4[10]), .reset(reset));  // open: Qn, preset, en
  D_Flip_Flop d_ff_12 (.clk(clock), .D(_16bit_input[11]), .Q(out_4[11]), .reset(reset));  // open: Qn, preset, en
  D_Flip_Flop d_ff_13 (.clk(clock), .D(_16bit_input[12]), .Q(out_4[12]), .reset(reset));  // open: Qn, preset, en
  D_Flip_Flop d_ff_14 (.clk(clock), .D(_16bit_input[13]), .Q(out_4[13]), .reset(reset));  // open: Qn, preset, en
  D_Flip_Flop d_ff_15 (.clk(clock), .D(_16bit_input[14]), .Q(out_4[14]), .reset(reset));  // open: Qn, preset, en
  D_Flip_Flop d_ff_16 (.clk(clock), .D(_16bit_input[15]), .Q(out_4[15]), .reset(reset));  // open: Qn, preset, en
endmodule

module _16_x_16 (
  input  [15:0] in_1,
  input  [15:0] in_2,
  input  [15:0] in_3,
  input  [15:0] in_4,
  input  [15:0] in_5,
  input  [15:0] in_6,
  input  [15:0] in_7,
  input  [15:0] in_8,
  input  [15:0] in_9,
  input  [15:0] in_10,
  input  [15:0] in_11,
  input  [15:0] in_12,
  input  [15:0] in_13,
  input  [15:0] in_14,
  input  [15:0] in_15,
  input  [15:0] in_16,
  input  clk,
  input  rst,
  input  [3:0] in_19,
  output [15:0] out_20,
  output [15:0] out_21,
  output [15:0] out_22,
  output [15:0] out_23,
  output [15:0] out_24,
  output [15:0] out_25,
  output [15:0] out_26,
  output [15:0] out_27,
  output [15:0] out_28,
  output [15:0] out_29,
  output [15:0] out_30,
  output [15:0] out_31,
  output [15:0] out_32,
  output [15:0] out_33,
  output [15:0] out_34,
  output [15:0] out_35
);

  wire demultiplexer_1_out0, demultiplexer_1_out1, demultiplexer_1_out2, demultiplexer_1_out3,
       demultiplexer_1_out4, demultiplexer_1_out5, demultiplexer_1_out6, demultiplexer_1_out7,
       demultiplexer_1_out8, demultiplexer_1_out9, demultiplexer_1_out10, demultiplexer_1_out11,
       demultiplexer_1_out12, demultiplexer_1_out13, demultiplexer_1_out14, demultiplexer_1_out15;

  Demultiplexer #(.select(4)) demultiplexer_1 (
    .out0(demultiplexer_1_out0), .out1(demultiplexer_1_out1), .out2(demultiplexer_1_out2),
    .out3(demultiplexer_1_out3), .out4(demultiplexer_1_out4), .out5(demultiplexer_1_out5),
    .out6(demultiplexer_1_out6), .out7(demultiplexer_1_out7), .out8(demultiplexer_1_out8),
    .out9(demultiplexer_1_out9), .out10(demultiplexer_1_out10), .out11(demultiplexer_1_out11),
    .out12(demultiplexer_1_out12), .out13(demultiplexer_1_out13), .out14(demultiplexer_1_out14),
    .out15(demultiplexer_1_out15), .in(clk), .sel(in_19));  // open: en
  _16_bit_register u_16_bit_register_1 (._16bit_input(in_1), .clock(demultiplexer_1_out0), .reset(rst), .out_4(out_20));
  _16_bit_register u_16_bit_register_2 (._16bit_input(in_2), .clock(demultiplexer_1_out1), .reset(rst), .out_4(out_21));
  _16_bit_register u_16_bit_register_3 (._16bit_input(in_3), .clock(demultiplexer_1_out2), .reset(rst), .out_4(out_22));
  _16_bit_register u_16_bit_register_4 (._16bit_input(in_4), .clock(demultiplexer_1_out3), .reset(rst), .out_4(out_23));
  _16_bit_register u_16_bit_register_5 (._16bit_input(in_5), .clock(demultiplexer_1_out4), .reset(rst), .out_4(out_24));
  _16_bit_register u_16_bit_register_6 (._16bit_input(in_6), .clock(demultiplexer_1_out5), .reset(rst), .out_4(out_25));
  _16_bit_register u_16_bit_register_7 (._16bit_input(in_7), .clock(demultiplexer_1_out6), .reset(rst), .out_4(out_26));
  _16_bit_register u_16_bit_register_8 (._16bit_input(in_8), .clock(demultiplexer_1_out7), .reset(rst), .out_4(out_27));
  _16_bit_register u_16_bit_register_9 (._16bit_input(in_9), .clock(demultiplexer_1_out8), .reset(rst), .out_4(out_28));
  _16_bit_register u_16_bit_register_10 (
    ._16bit_input(in_10), .clock(demultiplexer_1_out9), .reset(rst), .out_4(out_29));
  _16_bit_register u_16_bit_register_11 (
    ._16bit_input(in_11), .clock(demultiplexer_1_out10), .reset(rst), .out_4(out_30));
  _16_bit_register u_16_bit_register_12 (
    ._16bit_input(in_12), .clock(demultiplexer_1_out11), .reset(rst), .out_4(out_31));
  _16_bit_register u_16_bit_register_13 (
    ._16bit_input(in_13), .clock(demultiplexer_1_out12), .reset(rst), .out_4(out_32));
  _16_bit_register u_16_bit_register_14 (
    ._16bit_input(in_14), .clock(demultiplexer_1_out13), .reset(rst), .out_4(out_33));
  _16_bit_register u_16_bit_register_15 (
    ._16bit_input(in_15), .clock(demultiplexer_1_out14), .reset(rst), .out_4(out_34));
  _16_bit_register u_16_bit_register_16 (
    ._16bit_input(in_16), .clock(demultiplexer_1_out15), .reset(rst), .out_4(out_35));
endmodule

module _16_x_16_row_update (
  input  [15:0] in_1,
  input  [15:0] in_2,
  input  [15:0] in_3,
  input  [15:0] in_4,
  input  [15:0] in_5,
  input  [15:0] in_6,
  input  [15:0] in_7,
  input  [15:0] in_8,
  input  [15:0] in_9,
  input  [15:0] in_10,
  input  [15:0] in_11,
  input  [15:0] in_12,
  input  [15:0] in_13,
  input  [15:0] in_14,
  input  [15:0] in_15,
  input  [15:0] in_16,
  input  clk,
  input  rst,
  output [15:0] out_19,
  output [15:0] out_20,
  output [15:0] out_21,
  output [15:0] out_22,
  output [15:0] out_23,
  output [15:0] out_24,
  output [15:0] out_25,
  output [15:0] out_26,
  output [15:0] out_27,
  output [15:0] out_28,
  output [15:0] out_29,
  output [15:0] out_30,
  output [15:0] out_31,
  output [15:0] out_32,
  output [15:0] out_33,
  output [15:0] out_34
);

  _16_bit_register u_16_bit_register_1 (._16bit_input(in_1), .clock(clk), .reset(rst), .out_4(out_19));
  _16_bit_register u_16_bit_register_2 (._16bit_input(in_2), .clock(clk), .reset(rst), .out_4(out_20));
  _16_bit_register u_16_bit_register_3 (._16bit_input(in_3), .clock(clk), .reset(rst), .out_4(out_21));
  _16_bit_register u_16_bit_register_4 (._16bit_input(in_4), .clock(clk), .reset(rst), .out_4(out_22));
  _16_bit_register u_16_bit_register_5 (._16bit_input(in_5), .clock(clk), .reset(rst), .out_4(out_23));
  _16_bit_register u_16_bit_register_6 (._16bit_input(in_6), .clock(clk), .reset(rst), .out_4(out_24));
  _16_bit_register u_16_bit_register_7 (._16bit_input(in_7), .clock(clk), .reset(rst), .out_4(out_25));
  _16_bit_register u_16_bit_register_8 (._16bit_input(in_8), .clock(clk), .reset(rst), .out_4(out_26));
  _16_bit_register u_16_bit_register_9 (._16bit_input(in_9), .clock(clk), .reset(rst), .out_4(out_27));
  _16_bit_register u_16_bit_register_10 (._16bit_input(in_10), .clock(clk), .reset(rst), .out_4(out_28));
  _16_bit_register u_16_bit_register_11 (._16bit_input(in_11), .clock(clk), .reset(rst), .out_4(out_29));
  _16_bit_register u_16_bit_register_12 (._16bit_input(in_12), .clock(clk), .reset(rst), .out_4(out_30));
  _16_bit_register u_16_bit_register_13 (._16bit_input(in_13), .clock(clk), .reset(rst), .out_4(out_31));
  _16_bit_register u_16_bit_register_14 (._16bit_input(in_14), .clock(clk), .reset(rst), .out_4(out_32));
  _16_bit_register u_16_bit_register_15 (._16bit_input(in_15), .clock(clk), .reset(rst), .out_4(out_33));
  _16_bit_register u_16_bit_register_16 (._16bit_input(in_16), .clock(clk), .reset(rst), .out_4(out_34));
endmodule
