// Logisim project Direction control.circ as structural Verilog: 1 circuit, main circuit Direction
module Direction (
  input  CLC,
  input  MS,
  input  RST,
  input  L,
  input  R,
  output [7:0] out_6,
  output [7:0] Head_location_output
);

  wire and_1_out, and_2_out, and_3_out, controlled_buffer_7_out, controlled_buffer_8_out,
       demultiplexer_1_out0, demultiplexer_1_out1, demultiplexer_1_out2, demultiplexer_1_out3, not_1_out,
       not_2_out, not_3_out, or_1_out, or_2_out, or_3_out, or_4_out, or_5_out, or_6_out, register_1_q,
       register_2_q, register_3_q, register_4_q, s_r_ff_1_q, s_r_ff_2_q;
  wire [1:0] FD;
  wire [3:0] adder_1_out, adder_2_out, subtractor_1_out, subtractor_2_out;
  wire [5:0] rom_1_data;

  Register #(.width(1)) register_1 (.D(L), .Q(register_1_q), .clk(CLC), .clr(RST));  // open: en
  Register #(.width(1)) register_2 (.D(R), .Q(register_2_q), .clk(CLC), .clr(RST));  // open: en
  S_R_Flip_Flop s_r_ff_1 (.Q(s_r_ff_1_q), .preset(L), .reset(or_1_out));  // open: S, clk, R, Qn, en
  or or_1 (or_1_out, and_1_out, register_3_q);
  and and_1 (and_1_out, L, register_1_q);
  S_R_Flip_Flop s_r_ff_2 (.Q(s_r_ff_2_q), .preset(R), .reset(or_2_out));  // open: S, clk, R, Qn, en
  or or_2 (or_2_out, and_2_out, register_4_q);
  and and_2 (and_2_out, R, register_2_q);
  Register #(.width(1)) register_3 (.D(s_r_ff_1_q), .Q(register_3_q), .clk(CLC), .clr(and_3_out));  // open: en
  Register #(.width(1)) register_4 (.D(s_r_ff_2_q), .Q(register_4_q), .clk(CLC), .clr(and_3_out));  // open: en
  ROM #(.addrWidth(2), .dataWidth(6)) rom_1 (.addr(FD), .data(rom_1_data));  // open: sel
  not not_1 (not_1_out, register_4_q);
  or or_3 (or_3_out, register_3_q, not_1_out);
  or or_4 (or_4_out, register_4_q, register_3_q);
  and and_3 (and_3_out, or_4_out, CLC);
  Counter #(.width(2), .max('h3)) counter_1 (
    .load(or_3_out), .count(1'b1), .Q(FD), .clk(and_3_out), .clr(RST));  // open: D, carry
  assign out_6[7:4] = rom_1_data[0] ? Head_location_output[7:4] : 4'bz;  // Controlled_Buffer controlled_buffer_1
  Adder #(.width(4)) adder_1 (.a(Head_location_output[7:4]), .b(4'b0001), .out(adder_1_out));  // open: cin, cout
  assign out_6[7:4] = rom_1_data[1] ? adder_1_out : 4'bz;  // Controlled_Buffer controlled_buffer_2
  Subtractor #(.width(4)) subtractor_1 (
    .a(Head_location_output[7:4]), .b(4'b0001), .out(subtractor_1_out));  // open: bin, bout
  assign out_6[7:4] = rom_1_data[2] ? subtractor_1_out : 4'bz;  // Controlled_Buffer controlled_buffer_3
  assign out_6[3:0] = rom_1_data[3] ? Head_location_output[3:0] : 4'bz;  // Controlled_Buffer controlled_buffer_4
  Adder #(.width(4)) adder_2 (.a(Head_location_output[3:0]), .b(4'b0001), .out(adder_2_out));  // open: cin, cout
  assign out_6[3:0] = rom_1_data[4] ? adder_2_out : 4'bz;  // Controlled_Buffer controlled_buffer_5
  assign out_6[3:0] = rom_1_data[5] ? subtractor_2_out : 4'bz;  // Controlled_Buffer controlled_buffer_6
  Subtractor #(.width(4)) subtractor_2 (
    .a(Head_location_output[3:0]), .b(4'b0001), .out(subtractor_2_out));  // open: bin, bout
  Demultiplexer #(.select(2)) demultiplexer_1 (
    .out0(demultiplexer_1_out0), .out1(demultiplexer_1_out1), .out2(demultiplexer_1_out2),
    .out3(demultiplexer_1_out3), .in(1'b1), .sel(FD));  // open: en
  or or_5 (or_5_out, demultiplexer_1_out0, demultiplexer_1_out2);
  or or_6 (or_6_out, demultiplexer_1_out1, demultiplexer_1_out2);
  not not_2 (not_2_out, or_5_out);
  assign controlled_buffer_7_out = or_5_out ? MS : 1'bz;  // Controlled_Buffer controlled_buffer_7
  not not_3 (not_3_out, demultiplexer_1_out3);
  assign controlled_buffer_8_out = not_2_out ? MS : 1'bz;  // Controlled_Buffer controlled_buffer_8
  Counter #(.width(4), .max('hf)) counter_2 (
    .load(or_6_out), .count(1'b1), .Q(Head_location_output[3:0]), .clk(controlled_buffer_7_out), .clr(RST));  // open: D, carry
  Counter #(.width(4), .max('hf)) counter_3 (
    .load(not_3_out), .count(1'b1), .Q(Head_location_output[7:4]), .clk(controlled_buffer_8_out), .clr(RST));  // open: D, carry

  // Other names for the same wires on the sheet: B[3:0] = Head_location_output[3:0];
  //   A[3:0] = Head_location_output[7:4]

  // Notes on the sheet:
  //   contents of rom_1 (hex, n*v repeats v):
  //   11 21 c a
endmodule
