// Logisim project Gamelogic.circ as structural Verilog: 1 circuit, main circuit main
module main (
  input  [7:0] Dot_y_x_data,
  input  [7:0] Head_x_y_data,
  input  [15:0] body_vector,
  input  [3:0] in_4,
  input  Check_clk,
  input  [15:0] in_6
);

  wire and_3_out, and_4_out, comparator_1_eq, comparator_2_eq, comparator_3_eq, comparator_4_gt,
       comparator_5_gt, not_1_out, not_2_out, or_2_out, or_3_out;
  wire [15:0] and_1_out, and_2_out, decoder_1_out15, decoder_2_out15, Dot_Filtered, Dot_filtered_t,
       Head_filtered;

  Decoder #(.select(4)) decoder_1 (
    .out0(decoder_1_out15[15]), .out1(decoder_1_out15[14]), .out2(decoder_1_out15[13]),
    .out3(decoder_1_out15[12]), .out4(decoder_1_out15[11]), .out5(decoder_1_out15[10]),
    .out6(decoder_1_out15[9]), .out7(decoder_1_out15[8]), .out8(decoder_1_out15[7]),
    .out9(decoder_1_out15[6]), .out10(decoder_1_out15[5]), .out11(decoder_1_out15[4]),
    .out12(decoder_1_out15[3]), .out13(decoder_1_out15[2]), .out14(decoder_1_out15[1]),
    .out15(decoder_1_out15[0]), .sel(Dot_y_x_data[3:0]));  // open: en
  Comparator #(.width(4)) comparator_1 (.a(Dot_y_x_data[7:4]), .b(in_4), .eq(comparator_1_eq));  // open: gt, lt
  Decoder #(.select(4)) decoder_2 (
    .out0(decoder_2_out15[15]), .out1(decoder_2_out15[14]), .out2(decoder_2_out15[13]),
    .out3(decoder_2_out15[12]), .out4(decoder_2_out15[11]), .out5(decoder_2_out15[10]),
    .out6(decoder_2_out15[9]), .out7(decoder_2_out15[8]), .out8(decoder_2_out15[7]),
    .out9(decoder_2_out15[6]), .out10(decoder_2_out15[5]), .out11(decoder_2_out15[4]),
    .out12(decoder_2_out15[3]), .out13(decoder_2_out15[2]), .out14(decoder_2_out15[1]),
    .out15(decoder_2_out15[0]), .sel(Head_x_y_data[3:0]));  // open: en
  Comparator #(.width(4)) comparator_2 (.a(Head_x_y_data[7:4]), .b(in_4), .eq(comparator_2_eq));  // open: gt, lt
  assign in_6 = Dot_Filtered | Head_filtered | body_vector;  // OR_Gate or_1, 16 bits wide
  not not_1 (not_1_out, comparator_1_eq);
  not not_2 (not_2_out, comparator_2_eq);
  Multiplexer #(.width(16)) multiplexer_1 (
    .in0(decoder_1_out15), .in1({16{1'b0}}), .out(Dot_filtered_t), .sel(not_1_out));  // open: en
  Multiplexer #(.width(16)) multiplexer_2 (
    .in0(decoder_2_out15), .in1({16{1'b0}}), .out(Head_filtered), .sel(not_2_out));  // open: en
  assign and_1_out = Head_filtered & body_vector;  // AND_Gate and_1, 16 bits wide
  assign and_2_out = body_vector & Dot_filtered_t;  // AND_Gate and_2, 16 bits wide
  Comparator comparator_3 (.a(Dot_y_x_data), .b(Head_x_y_data), .eq(comparator_3_eq));  // open: gt, lt
  Comparator #(.width(16)) comparator_4 (.a(and_1_out), .b({16{1'b0}}), .gt(comparator_4_gt));  // open: eq, lt
  Comparator #(.width(16)) comparator_5 (.a(and_2_out), .b({16{1'b0}}), .gt(comparator_5_gt));  // open: eq, lt
  and and_3 (and_3_out, comparator_4_gt, Check_clk);
  and and_4 (and_4_out, comparator_5_gt, Check_clk);
  or or_2 (or_2_out, 1'b0, and_3_out);
  // Probe on or_2_out
  or or_3 (or_3_out, 1'b0, and_4_out);
  // Probe on or_3_out
  // Probe on comparator_3_eq

  // Other names for the same wires on the sheet: Body[15:0] = body_vector; clc = Check_clk; Dot[7:0] = Dot_y_x_data;
  //   Head[7:0] = Head_x_y_data; Rank[3:0] = in_4

  // Notes on the sheet:
  //   Inputs is routed to tunnels
  //   Current Rank being read
  //   Check for loss condition
  //   Sends dot, head and body to display
  //   If (dot rank == body rank) assign decoded dot position, otherwise assign 0000
  //   If (head rank == body rank) assign decoded dot position, otherwise assign 0000
  //   Display
  //   If the head overlaps a body pixel, send a game over signal
  //   If the random dot is placed on the body, send an error signal
  //   If the random dot overlaps the head pixel, send a point signal
endmodule
