// Logisim project Random Dot Generator.circ as structural Verilog: 1 circuit, main circuit main
module main (
  input  in_1,
  input  in_2,
  output [15:0] out_3,
  output [15:0] out_4,
  output [15:0] out_5,
  output [15:0] out_6,
  output [15:0] out_7,
  output [15:0] out_8,
  output [15:0] out_9,
  output [15:0] out_10,
  output [15:0] out_11,
  output [15:0] out_12,
  output [15:0] out_13,
  output [15:0] out_14,
  output [15:0] out_15,
  output [15:0] out_16,
  output [15:0] out_17,
  output [15:0] out_18,
  output [7:0] out_19
);

  wire demultiplexer_1_out0, demultiplexer_1_out1, demultiplexer_1_out2, demultiplexer_1_out3,
       demultiplexer_1_out4, demultiplexer_1_out5, demultiplexer_1_out6, demultiplexer_1_out7,
       demultiplexer_1_out8, demultiplexer_1_out9, demultiplexer_1_out10, demultiplexer_1_out11,
       demultiplexer_1_out12, demultiplexer_1_out13, demultiplexer_1_out14, demultiplexer_1_out15;
  wire [15:0] demultiplexer_2_out15;

  Random #(.width(4), .seed(5)) random_1 (.clk(in_1), .out(out_19[7:4]));  // open: next, clr
  Random #(.width(4)) random_2 (.clk(in_1), .out(out_19[3:0]));  // open: next, clr
  Demultiplexer #(.select(4)) demultiplexer_1 (
    .out0(demultiplexer_1_out0), .out1(demultiplexer_1_out1), .out2(demultiplexer_1_out2),
    .out3(demultiplexer_1_out3), .out4(demultiplexer_1_out4), .out5(demultiplexer_1_out5),
    .out6(demultiplexer_1_out6), .out7(demultiplexer_1_out7), .out8(demultiplexer_1_out8),
    .out9(demultiplexer_1_out9), .out10(demultiplexer_1_out10), .out11(demultiplexer_1_out11),
    .out12(demultiplexer_1_out12), .out13(demultiplexer_1_out13), .out14(demultiplexer_1_out14),
    .out15(demultiplexer_1_out15), .in(in_2), .sel(out_19[3:0]));  // open: en
  Demultiplexer #(.select(4)) demultiplexer_2 (
    .out0(demultiplexer_2_out15[15]), .out1(demultiplexer_2_out15[14]), .out2(demultiplexer_2_out15[13]),
    .out3(demultiplexer_2_out15[12]), .out4(demultiplexer_2_out15[11]), .out5(demultiplexer_2_out15[10]),
    .out6(demultiplexer_2_out15[9]), .out7(demultiplexer_2_out15[8]), .out8(demultiplexer_2_out15[7]),
    .out9(demultiplexer_2_out15[6]), .out10(demultiplexer_2_out15[5]), .out11(demultiplexer_2_out15[4]),
    .out12(demultiplexer_2_out15[3]), .out13(demultiplexer_2_out15[2]), .out14(demultiplexer_2_out15[1]),
    .out15(demultiplexer_2_out15[0]), .in(1'b1), .sel(out_19[7:4]), .en(in_2));
  assign out_3 = demultiplexer_1_out0 ? demultiplexer_2_out15 : 16'bz;  // Controlled_Buffer controlled_buffer_1
  assign out_4 = demultiplexer_1_out1 ? demultiplexer_2_out15 : 16'bz;  // Controlled_Buffer controlled_buffer_2
  assign out_5 = demultiplexer_1_out2 ? demultiplexer_2_out15 : 16'bz;  // Controlled_Buffer controlled_buffer_3
  assign out_6 = demultiplexer_1_out3 ? demultiplexer_2_out15 : 16'bz;  // Controlled_Buffer controlled_buffer_4
  assign out_7 = demultiplexer_1_out4 ? demultiplexer_2_out15 : 16'bz;  // Controlled_Buffer controlled_buffer_5
  assign out_8 = demultiplexer_1_out5 ? demultiplexer_2_out15 : 16'bz;  // Controlled_Buffer controlled_buffer_6
  assign out_9 = demultiplexer_1_out6 ? demultiplexer_2_out15 : 16'bz;  // Controlled_Buffer controlled_buffer_7
  assign out_10 = demultiplexer_1_out7 ? demultiplexer_2_out15 : 16'bz;  // Controlled_Buffer controlled_buffer_8
  assign out_11 = demultiplexer_1_out8 ? demultiplexer_2_out15 : 16'bz;  // Controlled_Buffer controlled_buffer_9
  assign out_12 = demultiplexer_1_out9 ? demultiplexer_2_out15 : 16'bz;  // Controlled_Buffer controlled_buffer_10
  assign out_13 = demultiplexer_1_out10 ? demultiplexer_2_out15 : 16'bz;  // Controlled_Buffer controlled_buffer_11
  assign out_14 = demultiplexer_1_out11 ? demultiplexer_2_out15 : 16'bz;  // Controlled_Buffer controlled_buffer_12
  assign out_15 = demultiplexer_1_out12 ? demultiplexer_2_out15 : 16'bz;  // Controlled_Buffer controlled_buffer_13
  Controlled_Buffer #(.width(16)) controlled_buffer_14 (.out(out_16), .en(demultiplexer_1_out13));  // open: in
  assign out_17 = demultiplexer_1_out14 ? demultiplexer_2_out15 : 16'bz;  // Controlled_Buffer controlled_buffer_15
  assign out_18 = demultiplexer_1_out15 ? demultiplexer_2_out15 : 16'bz;  // Controlled_Buffer controlled_buffer_16

  // Other names for the same wires on the sheet: B[3:0] = out_19[3:0]; A[3:0] = out_19[7:4]
endmodule
