// Logisim project snake.circ as structural Verilog: 1 circuit, main circuit main
module main (
  input  in_1,
  output [7:0] out_2,
  output [7:0] out_3
);

  wire _0, _1, _2, _3, _4, _5, _6, _7, _8, _9, _10, _11, _12, _13, _14, _15, clock_1_out, comparator_1_eq,
       comparator_2_eq, comparator_3_eq, comparator_4_gt, E, L, not_1_out, or_1_out, or_3_out, or_4_out, RST,
       tunnel;
  wire [3:0] counter_3_q, Rank, subtractor_1_out;
  wire [6:0] Keyboard_out;
  wire [7:0] adder_1_out, counter_4_q, Dot, multiplexer_1_out, multiplexer_2_out, ram_1_data, rom_1_data,
       Score, subtractor_3_out;
  wire [8:0] counter_2_q;
  wire [15:0] Body, demultiplexer_1_out0, demultiplexer_1_out1, demultiplexer_1_out2, demultiplexer_1_out3,
       demultiplexer_1_out4, demultiplexer_1_out5, demultiplexer_1_out6, demultiplexer_1_out7,
       demultiplexer_1_out8, demultiplexer_1_out9, demultiplexer_1_out10, demultiplexer_1_out11,
       demultiplexer_1_out12, demultiplexer_1_out13, demultiplexer_1_out14, demultiplexer_1_out15,
       Display_line, n16_x_16_1_out_20, n16_x_16_1_out_21, n16_x_16_1_out_22, n16_x_16_1_out_23,
       n16_x_16_1_out_24, n16_x_16_1_out_25, n16_x_16_1_out_26, n16_x_16_1_out_27, n16_x_16_1_out_28,
       n16_x_16_1_out_29, n16_x_16_1_out_30, n16_x_16_1_out_31, n16_x_16_1_out_32, n16_x_16_1_out_33,
       n16_x_16_1_out_34, n16_x_16_1_out_35, n16_x_16_row_update_1_out_19, n16_x_16_row_update_1_out_20,
       n16_x_16_row_update_1_out_21, n16_x_16_row_update_1_out_22, n16_x_16_row_update_1_out_23,
       n16_x_16_row_update_1_out_24, n16_x_16_row_update_1_out_25, n16_x_16_row_update_1_out_26,
       n16_x_16_row_update_1_out_27, n16_x_16_row_update_1_out_28, n16_x_16_row_update_1_out_29,
       n16_x_16_row_update_1_out_30, n16_x_16_row_update_1_out_31, n16_x_16_row_update_1_out_32,
       n16_x_16_row_update_1_out_33, n16_x_16_row_update_1_out_34;

  or or_1 (or_1_out, RST, _8);
  Counter counter_1 (.Q(Score), .clk(tunnel), .clr(RST));  // open: load, D, count, carry
  Counter #(.width(9), .max('h1ff)) counter_2 (
    .Q(counter_2_q), .clk(comparator_3_eq), .clr(or_1_out));  // open: load, D, count, carry
  Counter counter_3 (.Q({Rank, counter_3_q}), .clk(_1), .clr(RST));  // open: load, D, count, carry
  Clock clock_1 (.out(clock_1_out));
  Comparator #(.width(7)) comparator_1 (.a(Keyboard_out), .b(7'b1100001), .eq(comparator_1_eq));  // open: gt, lt
  Comparator #(.width(7)) comparator_2 (.a(Keyboard_out), .b(7'b1100100), .eq(comparator_2_eq));  // open: gt, lt
  Adder adder_1 (.a(Score), .b(8'h2), .out(adder_1_out));  // open: cin, cout
  ROM #(.addrWidth(9)) rom_1 (.addr(counter_2_q), .data(rom_1_data));  // open: sel
  or or_2 (RST, in_1, L);
  Multiplexer #(.width(8), .enable("false")) multiplexer_1 (
    .in0({Rank, counter_3_q}), .in1(out_3), .out(multiplexer_1_out), .sel(_0));
  Multiplexer #(.width(8), .enable("false")) multiplexer_2 (
    .in0(subtractor_3_out), .in1(adder_1_out), .out(multiplexer_2_out), .sel(_0));
  not not_1 (not_1_out, comparator_3_eq);
  Counter counter_4 (
    .load(comparator_3_eq), .D(rom_1_data), .count(not_1_out), .Q(counter_4_q), .clk(clock_1_out), .clr(RST));  // open: carry
  or or_3 (or_3_out, tunnel, E);
  Random_Dot_Generator_main main_1 (
    .out_19(Dot), .in_1(or_3_out), .in_2(1'b1));  // open: out_3, out_4, out_5, out_6, out_7, out_8, out_9, out_10, out_11, out_12, out_13, out_14, out_15, out_16, out_17, out_18
  Direction direction_1 (
    .CLC(_7), .MS(_3), .Head_location_output(out_2), .RST(RST), .L(comparator_2_eq), .R(comparator_1_eq));  // open: out_6
  Comparator #(.width(16)) comparator_3 (
    .a({_15, _14, _13, _12, _11, _10, _9, _8, _7, _6, _5, _4, _3, _2, _1, _0}), .b({16{1'b0}}),
    .eq(comparator_3_eq));  // open: gt, lt
  RAM #(.bus("separate")) ram_1 (
    .addr(multiplexer_1_out), .din(multiplexer_2_out), .data(ram_1_data), .str(1'b1), .clk(_2), .ld(1'b1),
    .clr(RST));  // open: sel
  ROM #(.dataWidth(16)) rom_2 (
    .addr(counter_4_q), .data({_15, _14, _13, _12, _11, _10, _9, _8, _7, _6, _5, _4, _3, _2, _1, _0}));  // open: sel
  Subtractor #(.width(4)) subtractor_1 (.a(out_2[3:0]), .b(4'b0000), .out(subtractor_1_out));  // open: bin, bout
  Subtractor #(.width(4)) subtractor_2 (.a(out_2[7:4]), .b(4'b0001), .out(out_3[7:4]));  // open: bin, bout
  Comparator comparator_4 (.a(ram_1_data), .b({8{1'b0}}), .gt(comparator_4_gt));  // open: eq, lt
  Subtractor subtractor_3 (.a(ram_1_data), .b({8{1'b0}}), .out(subtractor_3_out), .bin(comparator_4_gt));  // open: bout
  not not_2 (out_3[0], subtractor_1_out[0]);
  not not_3 (out_3[1], subtractor_1_out[1]);
  not not_4 (out_3[2], subtractor_1_out[2]);
  not not_5 (out_3[3], subtractor_1_out[3]);
  Shift_Register #(.length(16)) shift_register_1 (
    .in(comparator_4_gt), .clk(_1), .clr(RST), .q0(Body[15]), .q1(Body[14]), .q2(Body[13]), .q3(Body[12]),
    .q4(Body[11]), .q5(Body[10]), .q6(Body[9]), .q7(Body[8]), .q8(Body[7]), .q9(Body[6]), .q10(Body[5]),
    .q11(Body[4]), .q12(Body[3]), .q13(Body[2]), .q14(Body[1]), .q15(Body[0]));  // open: shift, out, load, d0, d1, d2, d3, d4, d5, d6, d7, d8, d9, d10, d11, d12, d13, d14, d15
  Demultiplexer #(.select(4), .width(16)) demultiplexer_1 (
    .out0(demultiplexer_1_out0), .out1(demultiplexer_1_out1), .out2(demultiplexer_1_out2),
    .out3(demultiplexer_1_out3), .out4(demultiplexer_1_out4), .out5(demultiplexer_1_out5),
    .out6(demultiplexer_1_out6), .out7(demultiplexer_1_out7), .out8(demultiplexer_1_out8),
    .out9(demultiplexer_1_out9), .out10(demultiplexer_1_out10), .out11(demultiplexer_1_out11),
    .out12(demultiplexer_1_out12), .out13(demultiplexer_1_out13), .out14(demultiplexer_1_out14),
    .out15(demultiplexer_1_out15), .in(Display_line), .sel(Rank));  // open: en
  or or_4 (or_4_out, _9, RST);
  _16_x_16 u_16_x_16_1 (
    .in_1(demultiplexer_1_out0), .in_2(demultiplexer_1_out1), .in_3(demultiplexer_1_out2),
    .in_4(demultiplexer_1_out3), .in_5(demultiplexer_1_out4), .in_6(demultiplexer_1_out5),
    .in_7(demultiplexer_1_out6), .in_8(demultiplexer_1_out7), .in_9(demultiplexer_1_out8),
    .in_10(demultiplexer_1_out9), .in_11(demultiplexer_1_out10), .in_12(demultiplexer_1_out11),
    .in_13(demultiplexer_1_out12), .in_14(demultiplexer_1_out13), .in_15(demultiplexer_1_out14),
    .in_16(demultiplexer_1_out15), .clk(_5), .rst(or_4_out), .in_19(Rank), .out_20(n16_x_16_1_out_20),
    .out_21(n16_x_16_1_out_21), .out_22(n16_x_16_1_out_22), .out_23(n16_x_16_1_out_23),
    .out_24(n16_x_16_1_out_24), .out_25(n16_x_16_1_out_25), .out_26(n16_x_16_1_out_26),
    .out_27(n16_x_16_1_out_27), .out_28(n16_x_16_1_out_28), .out_29(n16_x_16_1_out_29),
    .out_30(n16_x_16_1_out_30), .out_31(n16_x_16_1_out_31), .out_32(n16_x_16_1_out_32),
    .out_33(n16_x_16_1_out_33), .out_34(n16_x_16_1_out_34), .out_35(n16_x_16_1_out_35));
  Gamelogic_main main_2 (
    .Dot_y_x_data(Dot), .Head_x_y_data(out_2), .body_vector(Body), .in_4(Rank), .Check_clk(_5), .out_6(L),
    .out_7(E), .out_9(tunnel), .out_8(Display_line));
  _16_x_16_row_update u_16_x_16_row_update_1 (
    .in_1(n16_x_16_1_out_20), .in_2(n16_x_16_1_out_21), .in_3(n16_x_16_1_out_22), .in_4(n16_x_16_1_out_23),
    .in_5(n16_x_16_1_out_24), .in_6(n16_x_16_1_out_25), .in_7(n16_x_16_1_out_26), .in_8(n16_x_16_1_out_27),
    .in_9(n16_x_16_1_out_28), .in_10(n16_x_16_1_out_29), .in_11(n16_x_16_1_out_30),
    .in_12(n16_x_16_1_out_31), .in_13(n16_x_16_1_out_32), .in_14(n16_x_16_1_out_33),
    .in_15(n16_x_16_1_out_34), .in_16(n16_x_16_1_out_35), .clk(_6), .rst(RST),
    .out_19(n16_x_16_row_update_1_out_19), .out_20(n16_x_16_row_update_1_out_20),
    .out_21(n16_x_16_row_update_1_out_21), .out_22(n16_x_16_row_update_1_out_22),
    .out_23(n16_x_16_row_update_1_out_23), .out_24(n16_x_16_row_update_1_out_24),
    .out_25(n16_x_16_row_update_1_out_25), .out_26(n16_x_16_row_update_1_out_26),
    .out_27(n16_x_16_row_update_1_out_27), .out_28(n16_x_16_row_update_1_out_28),
    .out_29(n16_x_16_row_update_1_out_29), .out_30(n16_x_16_row_update_1_out_30),
    .out_31(n16_x_16_row_update_1_out_31), .out_32(n16_x_16_row_update_1_out_32),
    .out_33(n16_x_16_row_update_1_out_33), .out_34(n16_x_16_row_update_1_out_34));
  Hex_Digit_Display hex_digit_display_1 (.value(Score[7:4]));  // open: dp
  DotMatrix #(.inputtype("row"), .matrixcols(16), .matrixrows(16)) dotmatrix_1 (
    .row0(n16_x_16_row_update_1_out_19), .row1(n16_x_16_row_update_1_out_20),
    .row2(n16_x_16_row_update_1_out_21), .row3(n16_x_16_row_update_1_out_22),
    .row4(n16_x_16_row_update_1_out_23), .row5(n16_x_16_row_update_1_out_24),
    .row6(n16_x_16_row_update_1_out_25), .row7(n16_x_16_row_update_1_out_26),
    .row8(n16_x_16_row_update_1_out_27), .row9(n16_x_16_row_update_1_out_28),
    .row10(n16_x_16_row_update_1_out_29), .row11(n16_x_16_row_update_1_out_30),
    .row12(n16_x_16_row_update_1_out_31), .row13(n16_x_16_row_update_1_out_32),
    .row14(n16_x_16_row_update_1_out_33), .row15(n16_x_16_row_update_1_out_34));
  Keyboard keyboard_1 (.clk(_7), .data(Keyboard_out));  // open: re, clr, avail
  Hex_Digit_Display hex_digit_display_2 (.value(Score[3:0]));  // open: dp
  Hex_Digit_Display hex_digit_display_3 (.value(Dot[7:4]));  // open: dp
  Hex_Digit_Display hex_digit_display_4 (.value(Dot[3:0]));  // open: dp
  Counter counter_5 (.clk(E));  // open: load, D, count, Q, carry, clr
  Counter counter_6 (.clk(tunnel));  // open: load, D, count, Q, carry, clr
  Hex_Digit_Display hex_digit_display_5 (.value(out_2[7:4]));  // open: dp
  Hex_Digit_Display hex_digit_display_6 (.value(out_2[3:0]));  // open: dp
  Counter counter_7 (.clk(L));  // open: load, D, count, Q, carry, clr

  // Other names for the same wires on the sheet: Head[7:0] = out_2; Head_1[7:0] = out_3

  // Notes on the sheet:
  //   contents of rom_1 (hex, n*v repeats v):
  //   0 4 28 4 28 4 28 4 28 4 28 4 28 4 28 4 28 4 28 4 28 4 28 4 28 4 28 4 28 4 28 4 28 2a ff
  //   contents of rom_2 (hex, n*v repeats v):
  //   81 d 0 0 6 10 6 10 6 10 6 10 6 10 6 10 6 10 6 10 6 10 6 10 6 10 6 10 6 10 6 10 6 10 6 10 4*0 20 0 40
  //   200 211*0 100
  //   Snake Built with Logisim
  //   Game logic
  //   Row update
  //   Final update
  //   A - D keyboard control
  //   // for debugging
endmodule
